# Fritzing sketch test (saved by Fritzing 0.9.2b)
breadboards: 1

parts:
  Part1 = Arduino Uno (Rev3)
  U1 = ATTINY13 [package=dip]
  C1 = Electrolytic Capacitor [capacitance=1µF package="100 mil [THT, electrolytic]"]
  S1 = Toggle Switch [package=THT]
  U2 = mystery part, 3 pins [chip_label=RX]
  Part2 = Arduino Micro (Rev3)

nets:
  N1: Part1.D10_PWM/SS, U1.PB5(NRES)
  N2: Part1.D11_PWM/MOSI, U1.PB0(MOSI)
  N3: Part1.D12/MISO, U1.PB1(MISO)
  N4: Part1.D13/SCK, U1.PB2(SCK_ADC1)
  GND: Part1.GND, U1.GND, C1.-, U2.pin1, Part2.GND
  5V: Part1.5V, U1.VCC, C1.+, U2.pin3
  TP2: U1.PB3(ADC3), S1.COM
  TP1: U1.PB4(ADC2), Part2.D0/RX
  N5: S1.L1, U2.pin2
  N6: S1.L2, Part2.D10_PWM/A10

notes:
  ATtiny RF testing, To test the code, a setup like this is used
